# Fritzing sketch WRO_FE_v4.5 (saved by Fritzing 1.0.3b)
circuit board: 7.26cm x 7.9cm
breadboards: 1

parts:
  TB6612FNG = Motor Driver 1A Dual TB6612FNG
  U3 = male pin header, 4 pins [form="♂ (male)"]
  U1 = male pin header, 4 pins [form="♂ (male)"]
  SERVO = KF301-2 [part_number=KF301-2 package="screwterminal-5mm 2 position"]
  U2 = male pin header, 4 pins [form="♂ (male)"]
  U4 = male pin header, 4 pins [form="♂ (male)"]
  MOTOR = Toggle Switch [package=THT]
  R3 = Resistor [tolerance=±5% power=0.25W resistance=220 package=THT]
  R2 = Resistor [tolerance=±5% power=0.25W resistance=220 package=THT]
  R1 = Resistor [tolerance=±5% power=0.25W resistance=220 package=THT]
  HMC5883L = Boladge HMC5883L Compass Module
  M_O/P = KF301-2 [part_number=KF301-2 package="screwterminal-5mm 2 position"]
  MAIN = KF301-2 [part_number=KF301-2 package="screwterminal-5mm 2 position"]
  VM = KF301-2 [part_number=KF301-2 package="screwterminal-5mm 2 position"]
  SERVO_2 = male pin header, 3 pins [form="♂ (male)"]
  RPI = double row female pin header, 40 pins [form="♀ (female)"]
  SERVO_3 = Toggle Switch [package=THT]
  START = Pushbutton [package="[THT]"]
  MAIN_2 = Toggle Switch [package=THT]
  U5 = male pin header, 4 pins [form="♂ (male)"]
  LED = RGB LED (com. cathode, rbg) [color="Red (633nm)" current=0.030A package="5 mm [THT]"]
  I2C_a = male pin header, 4 pins [form="♂ (male)"]
  I2C_b = male pin header, 4 pins [form="♂ (male)"]
  R4 = Resistor [tolerance=±5% power=0.25W resistance=1k package=THT]

nets:
  GND: TB6612FNG.GND, SERVO.2, HMC5883L.GND, MAIN.2, VM.2, SERVO_2.pin3, RPI.pin40, LED.common_cathode, I2C_a.pin2, I2C_b.pin2, R4.Pin_0
  N1: TB6612FNG.A02, M_O/P.2
  N2: TB6612FNG.A01, M_O/P.1
  N3: TB6612FNG.VCC, U3.pin4, U1.pin4, U2.pin4, U4.pin4, RPI.pin20, START.Pin_3, START.Pin_4, MAIN_2.COM, U5.pin4
  N4: TB6612FNG.VM, MOTOR.COM
  N5: TB6612FNG.PWMA, RPI.pin38
  N6: TB6612FNG.AIN2, RPI.pin2
  N7: TB6612FNG.AIN1, RPI.pin5
  N8: TB6612FNG.STBY, RPI.pin39
  N9: U3.pin1, U1.pin1, U2.pin1, U4.pin1, RPI.pin33, U5.pin1
  N10: U3.pin2, RPI.pin30
  N11: U3.pin3, RPI.pin31
  N12: U1.pin2, RPI.pin24
  N13: U1.pin3, RPI.pin26
  N14: SERVO.1, SERVO_3.L1
  N15: U2.pin2, RPI.pin27
  N16: U2.pin3, RPI.pin28
  N17: U4.pin2, RPI.pin36
  N18: U4.pin3, RPI.pin37
  N19: MOTOR.L1, VM.1
  N20: R3.Pin_0, RPI.pin17
  N21: R3.Pin_1, LED.red_anode
  N22: R2.Pin_0, RPI.pin16
  N23: R2.Pin_1, LED.blue_anode
  N24: R1.Pin_0, RPI.pin15
  N25: R1.Pin_1, LED.green_anode
  N26: HMC5883L.VCC, RPI.pin21, I2C_a.pin1, I2C_b.pin1
  N27: HMC5883L.SCL, RPI.pin23, I2C_a.pin3, I2C_b.pin3
  N28: HMC5883L.SDA, RPI.pin22, I2C_a.pin4, I2C_b.pin4
  N29: MAIN.1, MAIN_2.L1
  N30: SERVO_2.pin1, RPI.pin35
  N31: SERVO_2.pin2, SERVO_3.COM
  N32: RPI.pin1, U5.pin2
  N33: RPI.pin3, U5.pin3
  N34: RPI.pin12, RPI.pin13, START.Pin_1, START.Pin_2, R4.Pin_1

notes:
  GND
  VCC
  07
  11
  13
  15
  19
  21
  33
  31
  35
  38
  32
  37
  +12V
  29
  +V
  ON
  3V3
  5V
  SDA
  SCL
  8
  7
  10
  12
  16
  18
  22
  26
  23
  24
  27
  28
  36
  40

custom parts:
  KF301-2: KF301-3 is a 3 position screw terminal header block with male through hole PCB pins on 5mm spacing
  Boladge HMC5883L Compass Module: Cheap digital compass module
