# Fritzing sketch WRO_FE_PCB (saved by Fritzing 1.0.3b)
circuit board: 7.2cm x 8.2cm
breadboards: 1

parts:
  TB6612FNG = Motor Driver 1A Dual TB6612FNG
  GYRO = InvenSense MPU6050
  U3 = male pin header, 4 pins [form="♂ (male)"]
  U1 = male pin header, 4 pins [form="♂ (male)"]
  SERVO = KF301-2 [part_number=KF301-2 package="screwterminal-5mm 2 position"]
  U2 = male pin header, 4 pins [form="♂ (male)"]
  U4 = male pin header, 4 pins [form="♂ (male)"]
  MAIN = Toggle Switch [package=THT]
  MOTOR_SW = Toggle Switch [package=THT]
  R2 = Resistor [tolerance=±5% power=0.25W resistance=220 package=THT]
  R3 = Resistor [tolerance=±5% power=0.25W resistance=220 package=THT]
  R4 = Resistor [tolerance=±5% power=0.25W resistance=220 package=THT]
  HMC5883L = Boladge HMC5883L Compass Module
  M_O/P = KF301-2 [part_number=KF301-2 package="screwterminal-5mm 2 position"]
  MAIN_2 = KF301-2 [part_number=KF301-2 package="screwterminal-5mm 2 position"]
  VM = KF301-2 [part_number=KF301-2 package="screwterminal-5mm 2 position"]
  SERVO_2 = male pin header, 3 pins [form="♂ (male)"]
  LED = RGB LED (com. cathode, rbg) [color="Red (633nm)" current=0.030A package="5 mm [THT]"]
  RPI = double row female pin header, 40 pins [form="♀ (female)"]

nets:
  GND: TB6612FNG.GND, GYRO.GND, SERVO.2, HMC5883L.GND, MAIN_2.2, VM.2, SERVO_2.pin3, LED.blue_anode, RPI.pin18
  N1: TB6612FNG.A02, M_O/P.2
  N2: TB6612FNG.A01, M_O/P.1
  VCC: TB6612FNG.VCC, GYRO.VCC, U3.pin4, U1.pin4, U2.pin4, U4.pin4, MAIN.COM, RPI.pin20
  N3: TB6612FNG.VM, MOTOR_SW.COM
  N4: TB6612FNG.PWMA, RPI.pin38
  N5: TB6612FNG.AIN2, RPI.pin1
  N6: TB6612FNG.AIN1, RPI.pin3
  N7: TB6612FNG.STBY, RPI.pin39
  N8: GYRO.SCL, HMC5883L.SCL, RPI.pin23
  N9: GYRO.SDA, HMC5883L.SDA, RPI.pin22
  N10: U3.pin1, U1.pin1, U2.pin1, U4.pin1, RPI.pin33
  N11: U3.pin2, RPI.pin30
  N12: U3.pin3, RPI.pin31
  N13: U1.pin2, RPI.pin24
  N14: U1.pin3, RPI.pin26
  N15: SERVO.1, SERVO_2.pin2
  N16: U2.pin2, RPI.pin27
  N17: U2.pin3, RPI.pin28
  N18: U4.pin2, RPI.pin36
  N19: U4.pin3, RPI.pin37
  N20: MAIN.L1, MAIN_2.1
  N21: MOTOR_SW.L1, VM.1
  N22: R2.Pin_0, RPI.pin15
  N23: R2.Pin_1, LED.red_anode
  N24: R3.Pin_0, RPI.pin16
  N25: R3.Pin_1, LED.common_cathode
  N26: R4.Pin_0, RPI.pin17
  N27: R4.Pin_1, LED.green_anode
  N28: HMC5883L.VCC, RPI.pin21
  N29: SERVO_2.pin1, RPI.pin35

notes:
  GND
  TEAM MONKE
  VCC
  07
  11
  13
  15
  19
  21
  33
  31
  35
  40
  36
  37
  +12V
  29
  +V
  ON

custom parts:
  KF301-2: KF301-3 is a 3 position screw terminal header block with male through hole PCB pins on 5mm spacing
  Boladge HMC5883L Compass Module: Cheap digital compass module
