# Fritzing sketch WRO_FE_schematic (saved by Fritzing 1.0.3b)
circuit board: 7.2cm x 8.2cm
breadboards: 1

parts:
  TB6612FNG = Motor Driver 1A Dual TB6612FNG
  GYRO = InvenSense MPU6050
  U3 = male pin header, 4 pins [form="♂ (male)"]
  U1 = male pin header, 4 pins [form="♂ (male)"]
  SERVO = KF301-2 [part_number=KF301-2 package="screwterminal-5mm 2 position"]
  U2 = male pin header, 4 pins [form="♂ (male)"]
  U4 = male pin header, 4 pins [form="♂ (male)"]
  MAIN = Toggle Switch [package=THT]
  MOTOR_SW = Toggle Switch [package=THT]
  R2 = Resistor [tolerance=±5% power=0.25W resistance=220 package=THT]
  R3 = Resistor [tolerance=±5% power=0.25W resistance=220 package=THT]
  R4 = Resistor [tolerance=±5% power=0.25W resistance=220 package=THT]
  HMC5883L = Boladge HMC5883L Compass Module
  M_O/P = KF301-2 [part_number=KF301-2 package="screwterminal-5mm 2 position"]
  MAIN_2 = KF301-2 [part_number=KF301-2 package="screwterminal-5mm 2 position"]
  VM = KF301-2 [part_number=KF301-2 package="screwterminal-5mm 2 position"]
  SERVO_2 = male pin header, 3 pins [form="♂ (male)"]
  LED = RGB LED (com. cathode, rbg) [color="Red (633nm)" current=0.030A package="5 mm [THT]"]
  Mod1 = Raspberry Pi 4B
  S1 = SWITCH-MOMENTARY-2 [package=tactile_switch_smd-2]
  R5 = Resistor [tolerance=±5% power=0.25W resistance=1k package=THT]

nets:
  GND: TB6612FNG.GND, GYRO.GND, U3.pin1, U1.pin1, SERVO.2, U2.pin1, U4.pin1, HMC5883L.GND, MAIN_2.2, VM.2, SERVO_2.pin3, LED.common_cathode, Mod1.GND
  N1: TB6612FNG.A02, M_O/P.2
  N2: TB6612FNG.A01, M_O/P.1
  VCC: TB6612FNG.VCC, GYRO.VCC, U3.pin4, U1.pin4, U2.pin4, U4.pin4, MAIN.COM, Mod1.5V, S1.1
  N3: TB6612FNG.VM, MOTOR_SW.COM
  N4: TB6612FNG.PWMA, Mod1.GPIO19
  N5: TB6612FNG.AIN2, Mod1.GPIO21
  N6: TB6612FNG.AIN1, Mod1.GPIO16
  N7: TB6612FNG.STBY, Mod1.GPIO26
  N8: GYRO.SCL, HMC5883L.SCL, Mod1.GPIO3
  N9: GYRO.SDA, HMC5883L.SDA, Mod1.GPIO2
  N10: U3.pin2, Mod1.GPIO9
  N11: U3.pin3, Mod1.GPIO10
  N12: U1.pin2, Mod1.GPIO17
  N13: U1.pin3, Mod1.GPIO4
  N14: SERVO.1, SERVO_2.pin2
  N15: U2.pin2, Mod1.GPIO22
  N16: U2.pin3, Mod1.GPIO27
  N17: U4.pin2, Mod1.GPIO13
  N18: U4.pin3, Mod1.GPIO6
  N19: MAIN.L1, MAIN_2.1
  N20: MOTOR_SW.L1, VM.1
  N21: R2.Pin_0, Mod1.GPIO15
  N22: R2.Pin_1, LED.blue_anode
  N23: R3.Pin_0, Mod1.GPIO14
  N24: R3.Pin_1, LED.red_anode
  N25: R4.Pin_0, Mod1.GPIO18
  N26: R4.Pin_1, LED.green_anode
  VCC_2: HMC5883L.VCC, Mod1.3V3
  N27: SERVO_2.pin1, Mod1.GPIO5
  N28: Mod1.GPIO23, R5.Pin_0
  N29: S1.2, R5.Pin_1

notes:
  GND
  TEAM MONKE
  VCC
  07
  11
  13
  15
  19
  21
  33
  31
  35
  40
  36
  37
  +12V
  29
  +V
  ON

custom parts:
  KF301-2: KF301-3 is a 3 position screw terminal header block with male through hole PCB pins on 5mm spacing
  Boladge HMC5883L Compass Module: Cheap digital compass module
